# Fritzing sketch AutoFoto_v1.0 (saved by Fritzing 0.6.3b)
breadboards: 1

parts:
  Arduino1 = Arduino
  LED1 = LED - 5mm [color="Yellow (592nm)" package="5 mm [THT]"]
  LED2 = LED - 5mm [color="Red (633nm)" package="5 mm [THT]"]
  LED3 = LED - 5mm [color="Green (555nm)" package="5 mm [THT]"]
  J1 = female pin header, 3 pins [form="♀ (female)"]
  J2 = female pin header, 3 pins [form="♀ (female)"]
  U1 = Optocoupler [package=THT]
  U2 = Optocoupler [package=THT]
  R1 = Resistor [tolerance=±5% resistance=100 package=THT]
  R2 = Resistor [tolerance=±5% resistance=1k package=THT]
  R3 = Resistor [tolerance=±5% resistance=100 package=THT]
  R4 = Resistor [tolerance=±5% resistance=1k package=THT]

nets:
  N1: Arduino1.GND, LED1.cathode, LED2.cathode, LED3.cathode, J2.pin3, U1.Pin_2, U2.Pin_2
  N2: Arduino1.D13, LED1.anode
  N3: Arduino1.D12, J2.pin2
  N4: Arduino1.D10, R1.Pin_1, R2.Pin_1
  N5: Arduino1.D9, R3.Pin_1, R4.Pin_1
  N6: Arduino1.+5V, J2.pin1
  N7: LED2.anode, R2.Pin_0
  N8: LED3.anode, R4.Pin_0
  N9: J1.pin1, U2.Pin_5
  N10: J1.pin2, U1.Pin_5, U2.Pin_4
  N11: J1.pin3, U1.Pin_4
  N12: U1.Pin_1, R1.Pin_0
  N13: U2.Pin_1, R3.Pin_0

notes:
  Enable
  1 0
  Conector de camara
  Comun Foco Foto
